// Logisim project BFISA_VHDL.circ as structural Verilog: 4 circuits, main circuit main
module main (
  input  [7:0] Key
);

  wire and_1_out, and_2_out, and_3_out, and_4_out, Clk_out, comparator_1_gt, dbcr_pulse, decoder_hold,
       decoder_jump, decoder_loopback, decoder_memsrc, decoder_modmem, decoder_modptr, decoder_outp,
       Input_Valid_out, nor_1_out, nor_2_out, nor_3_out, nor_4_out, not_1_out, not_2_out, not_3_out,
       not_4_out, not_5_out, not_6_out, or_1_out, or_2_out, Reset_out, xor_1_out;
  wire [2:0] program_data;
  wire [6:0] mem_dout;
  wire [7:0] adder_3_out, multiplexer_3_out;
  wire [7:7] decoder_memop, mem_dout_2;
  wire [15:0] adder_1_out, adder_2_out, bit_extender_1_out, counter_1_q, multiplexer_1_out,
       multiplexer_2_out, PC_q, Pointer_q, register_1_q;
  wire [15:3] program_data_2;
  wire [15:15] decoder_ptrop;

  Clock Clk (.out(Clk_out));
  Button Reset (.out(Reset_out));
  Button Input_Valid (.out(Input_Valid_out));
  not not_1 (not_1_out, decoder_ptrop[15]);
  Comparator #(.width(16)) comparator_1 (
    .a(multiplexer_2_out), .b(register_1_q), .gt(comparator_1_gt));  // open: eq, lt
  Adder #(.width(16)) adder_1 (
    .a({16{decoder_ptrop[15]}}), .b(Pointer_q), .out(adder_1_out), .cin(not_1_out));  // open: cout
  Register #(.width(16)) register_1 (
    .D(multiplexer_2_out), .en(comparator_1_gt), .clk(Clk_out), .Q(register_1_q));  // open: clr
  Adder #(.width(16)) adder_2 (.a(PC_q), .b({16{1'b0}}), .out(adder_2_out), .cin(1'b1));  // open: cout
  Multiplexer #(.enable("false"), .width(16)) multiplexer_1 (
    .in0(adder_2_out), .in1(bit_extender_1_out), .out(multiplexer_1_out), .sel(and_1_out));
  and and_1 (and_1_out, xor_1_out, decoder_jump);
  xor xor_1 (xor_1_out, decoder_loopback, and_4_out);
  Debouncer dbcr (.Pulse(dbcr_pulse), .Buttn(Input_Valid_out), .Clk(Clk_out), .Rst(Reset_out));
  Decode decoder (
    .Opcode(program_data), .PtrOp(decoder_ptrop[15]), .MemOp(decoder_memop[7]), .LoopBack(decoder_loopback),
    .MemSrc(decoder_memsrc), .ModPtr(decoder_modptr), .Jump(decoder_jump), .Outp(decoder_outp),
    .ModMem(decoder_modmem), .Hold(decoder_hold));
  Register #(.width(16)) Pointer (.D(adder_1_out), .en(decoder_modptr), .clk(Clk_out), .Q(Pointer_q), .clr(Reset_out));
  or or_1 (or_1_out, dbcr_pulse, not_2_out);
  not not_2 (not_2_out, decoder_hold);
  Hex_Digit_Display hex_digit_display_1 (.value(register_1_q[15:12]));  // open: dp
  Register #(.width(16)) PC (.D(multiplexer_1_out), .en(or_1_out), .clk(Clk_out), .Q(PC_q), .clr(Reset_out));
  not not_3 (not_3_out, decoder_modptr);
  or or_2 (or_2_out, not_3_out, Clk_out);
  Multiplexer #(.enable("false"), .width(16)) multiplexer_2 (
    .in0(adder_1_out), .in1(Pointer_q), .out(multiplexer_2_out), .sel(or_2_out));
  Hex_Digit_Display hex_digit_display_2 (.value(register_1_q[11:8]));  // open: dp
  Hex_Digit_Display hex_digit_display_3 (.value(register_1_q[7:4]));  // open: dp
  ROM #(.addrWidth(16), .dataWidth(16)) \program  (.addr(PC_q), .data({program_data_2, program_data}));
  RAM #(.addrWidth(16)) mem (
    .addr(multiplexer_2_out), .we(decoder_modmem), .oe(1'b1), .clk(Clk_out), .din(multiplexer_3_out),
    .dout({mem_dout_2[7], mem_dout}));
  Hex_Digit_Display hex_digit_display_4 (.value(register_1_q[3:0]));  // open: dp
  not not_4 (not_4_out, Clk_out);
  TTY #(.cols(36), .rows(21)) tty_1 (.data(mem_dout), .clk(not_4_out), .we(decoder_outp), .clr(Reset_out));
  assign bit_extender_1_out = {{3{1'b0}}, program_data_2};  // Bit_Extender bit_extender_1
  not not_5 (not_5_out, decoder_memop[7]);
  Adder adder_3 (
    .a({mem_dout_2[7], mem_dout}), .b({8{decoder_memop[7]}}), .out(adder_3_out), .cin(not_5_out));  // open: cout
  nor nor_1 (nor_1_out, mem_dout[0], mem_dout[1]);
  and and_2 (and_2_out, nor_1_out, nor_2_out);
  nor nor_2 (nor_2_out, mem_dout[2], mem_dout[3]);
  nor nor_3 (nor_3_out, mem_dout[4], mem_dout[5]);
  and and_3 (and_3_out, nor_3_out, nor_4_out);
  nor nor_4 (nor_4_out, mem_dout[6], mem_dout_2[7]);
  Hex_Digit_Display hex_digit_display_5 (.value({mem_dout_2[7], mem_dout[6:4]}));  // open: dp
  Multiplexer #(.enable("false"), .width(8)) multiplexer_3 (
    .in0(adder_3_out), .in1(Key), .out(multiplexer_3_out), .sel(decoder_memsrc));
  Hex_Digit_Display hex_digit_display_6 (.value(multiplexer_3_out[7:4]));  // open: dp
  and and_4 (and_4_out, and_2_out, and_3_out);
  Hex_Digit_Display hex_digit_display_7 (.value(mem_dout[3:0]));  // open: dp
  Hex_Digit_Display hex_digit_display_8 (.value(multiplexer_3_out[3:0]));  // open: dp
  Hex_Digit_Display hex_digit_display_9 (.value(counter_1_q[15:12]));  // open: dp
  Counter #(.max('hffff), .width(16)) counter_1 (
    .clr(Reset_out), .load(1'b0), .up(1'b1), .count(not_6_out), .clk(Clk_out), .Q(counter_1_q));  // open: D, carry
  not not_6 (not_6_out, decoder_hold);
  Hex_Digit_Display hex_digit_display_10 (.value(counter_1_q[11:8]));  // open: dp
  Hex_Digit_Display hex_digit_display_11 (.value(counter_1_q[7:4]));  // open: dp
  Hex_Digit_Display hex_digit_display_12 (.value(counter_1_q[3:0]));  // open: dp

  // Notes on the sheet:
  //   contents of program (hex, n*v repeats v):
  //   0 1 4*0 2 2 0 2 0 2 2 0 2 0 0 2 2 1 1 1dcc 3 3 174 2 12c 2 2 2 4*1 3 3 d5 2 2 4*0 3 3 c5 2 1ac 4*1
  //   17d 0 20c 0 1f4 4*0 1c5 2 1 1b5 0 3 4*1 26c 4*1 23d 4*0 3bc 0 0 2d4 4*0 2a5 4*1 384 35c 4*0 2 4*1 3
  //   2fd 4*1 2f5 6*0 28d 0 0 3fc 4*0 3cd 4*1 45c 1 1 2 1 2 1 41d 1 1 a2c 6*0 534 50c 4*1 2 4*0 3 4ad 4*0
  //   4a5 8*1 5a4 4*1 575 0 0 3 5fc 1 1 2 0 0 3 5bd 2 1 1 7dc 3 4*0 784 3 694 2 4*0 3 655 3 1 1 3 6ec 4*0
  //   3 6b5 2 2 0 0 2 754 3 4*1 2 715 2 4*0 645 4*1 7d4 4*1 7a5 615 0 82c 3 824 1 2 0 3 7f5 7e5 2 1 a14 3
  //   4*0 9bc 3 8bc 2 4*0 3 87d 3 1 1 1 3 91c 4*0 3 8e5 2 2 0 0 0 2 98c 3 4*1 2 94d 2 4*0 86d 4*1 a0c 4*1
  //   9dd 83d 1 1 46d 0 0 0 2 a7c 4*0 a4d 3 acc 2 4*1 3 3 a85 2 2 b0c 4*1 add 0 0 0 2 1da4 0 3 df4 0 0 d2c
  //   3 3 bcc 2 2 0 0 2 0 0 3 3 b75 3 1 c8c 3 c84 3 c4c 2 2 2 4*1 3 bfd 2 4*0 3 bed bdd 2 2 0 2 cec 3 4*1
  //   2 cad 2 2 0 0 2 0 0 b5d 1 1 3 4*1 dc4 0 dac 1 3 1 1 1 d75 2 1 d65 0 3 0 0 0 b45 2 0 e34 4*0 e05 3
  //   e84 2 4*1 3 3 e3d 2 2 1 11d4 ed4 4*0 ea5 4*1 11cc 3 106c 3 0 3 3 f5c 1 3 0 2 f2d 2 2 1 102c fac 0 3
  //   1 2 f7d 2 2 fec 4*1 fbd 2 0 0 2 0 0 3 f75 2 2 4*1 3 f05 0 3 115c 2 10e4 1 2 10d4 4*1 10a5 0 108d 0 0
  //   0 1114 3 10fd 0 3 1154 1 2 0 3 1125 107d 2 1 119c 0 2 1 3 116d 2 4*1 ef5 e9d 0 120c 4*1 11dd 0 1bac
  //   3 1b4c 3 16b4 3 0 3 129c 1 1 2 0 2 0 3 1255 6*2 1334 1 8*2 0 3 12cd 1 6 3 3 1 138c 0 3 1 3 135d 5*0
  //   3 3 13dc 1 13c5 1 1 141c 1 1 6 1 13ed 0 143c 3 1425 0 0 3 0 0 2 2 1684 14ac 4*0 147d 2 1664 3 1634 3
  //   4*0 2 8*0 3 15ec 3 15b4 2 2 2 4*1 15ac 3 1595 1555 2 4*0 3 1545 2 2 162c 4*1 15fd 14c5 2 4*1 14b5 0
  //   0 0 1475 2 1 2 1 1 1235 0 1954 3 1944 3 0 18a4 3 3 174c 2 2 4*0 3 3 16fd 3 0 180c 3 1804 3 17cc 2 2
  //   2 4*1 3 177d 2 4*0 3 176d 175d 2 2 1 2 186c 3 4*1 2 182d 2 2 4*0 16e5 4*1 191c 0 1904 4*1 18d5 2 1
  //   18c5 0 3 0 0 16cd 1 16bd 4*0 1ae4 3 3 19dc 2 2 4*0 3 3 198d 3 1 3 3 1a54 2 2 2 4*0 3 3 19fd 2 0 2
  //   1aac 3 4*1 2 1a6d 2 2 4*0 1975 5*1 1b3c 4*1 1b0d 1 1225 0 1b9c 0 2 1 1 2 2 1 1b55 1 1215 0 1d8c 2 0
  //   1d3c 3 3 1c34 2 2 4*0 3 3 1be5 3 0 3 3 1cac 2 2 2 4*0 3 3 1c55 2 1 2 1d04 3 4*1 2 1cc5 2 2 4*0 1bcd
  //   1 1 1 1d84 4*1 1d55 1bb5 0 0 b2d 4*0 ad 7 6 7 6 ffff
endmodule

module Decode (
  input  [2:0] Opcode,
  output PtrOp,
  output MemOp,
  output LoopBack,
  output MemSrc,
  output ModPtr,
  output Jump,
  output Outp,
  output ModMem,
  output Hold
);

  wire and_1_out, and_2_out, nor_3_out, nor_4_out, not_1_out;

  not not_1 (not_1_out, Opcode[2]);
  nor nor_1 (ModPtr, Opcode[1], Opcode[2]);
  nor nor_2 (Jump, Opcode[1], not_1_out);
  nor nor_3 (nor_3_out, Opcode[0], not_1_out);
  and and_1 (and_1_out, Opcode[1], not_1_out);
  and and_2 (and_2_out, Opcode[0], Opcode[1]);
  and and_3 (Outp, nor_3_out, Opcode[1]);
  nor nor_4 (nor_4_out, and_1_out, and_2_out);
  not not_2 (ModMem, nor_4_out);
  and and_4 (Hold, and_2_out, Opcode[2]);

  assign LoopBack = Opcode[0];
  assign MemOp = Opcode[0];
  assign MemSrc = Opcode[2];
  assign PtrOp = Opcode[0];
endmodule

module Debouncer (
  input  Buttn,
  input  Clk,
  input  Rst,
  output Pulse
);

  wire d_ff_1_q, d_ff_2_q, d_ff_3_q, d_ff_4_q, d_ff_5_q, d_ff_6_q, d_ff_7_q, d_ff_8_q, nand_1_out,
       nand_2_out, nor_1_out;

  D_Flip_Flop d_ff_1 (.D(Buttn), .clk(Clk), .Q(d_ff_1_q), .reset(Rst));  // open: Qn, preset
  D_Flip_Flop d_ff_2 (.D(d_ff_1_q), .clk(Clk), .Q(d_ff_2_q), .reset(Rst));  // open: Qn, preset
  D_Flip_Flop d_ff_3 (.D(d_ff_2_q), .clk(Clk), .Q(d_ff_3_q), .reset(Rst));  // open: Qn, preset
  D_Flip_Flop d_ff_4 (.D(d_ff_3_q), .clk(Clk), .Q(d_ff_4_q), .reset(Rst));  // open: Qn, preset
  D_Flip_Flop d_ff_5 (.D(d_ff_4_q), .clk(Clk), .Q(d_ff_5_q), .reset(Rst));  // open: Qn, preset
  D_Flip_Flop d_ff_6 (.D(d_ff_5_q), .clk(Clk), .Q(d_ff_6_q), .reset(Rst));  // open: Qn, preset
  D_Flip_Flop d_ff_7 (.D(d_ff_6_q), .clk(Clk), .Q(d_ff_7_q), .reset(Rst));  // open: Qn, preset
  D_Flip_Flop d_ff_8 (.D(d_ff_7_q), .clk(Clk), .Q(d_ff_8_q), .reset(Rst));  // open: Qn, preset
  nor nor_1 (nor_1_out, d_ff_8_q, d_ff_8_q);
  nand nand_1 (nand_1_out, d_ff_7_q, d_ff_6_q, d_ff_5_q, d_ff_4_q);
  nand nand_2 (nand_2_out, d_ff_3_q, d_ff_2_q, d_ff_1_q, nor_1_out);
  nor nor_2 (Pulse, nand_1_out, nand_2_out);
endmodule

module main_synth (
  input  Clk,
  input  Rst,
  input  Input_valid,
  input  [7:0] Key,
  output [6:0] Char_out,
  output out_enable
);

  wire and_1_out, and_2_out, and_3_out, and_4_out, dbcr_pulse, decoder_hold, decoder_jump, decoder_loopback,
       decoder_memsrc, decoder_modmem, decoder_modptr, nor_1_out, nor_2_out, nor_3_out, nor_4_out, not_1_out,
       not_2_out, not_3_out, not_4_out, or_1_out, or_2_out, xor_1_out;
  wire [2:0] program_data;
  wire [7:0] adder_3_out, multiplexer_3_out;
  wire [7:7] decoder_memop, mem_dout;
  wire [15:0] adder_1_out, adder_2_out, bit_extender_1_out, multiplexer_1_out, multiplexer_2_out, PC_q,
       Pointer_q;
  wire [15:3] program_data_2;
  wire [15:15] decoder_ptrop;

  not not_1 (not_1_out, decoder_ptrop[15]);
  Adder #(.width(16)) adder_1 (
    .a({16{decoder_ptrop[15]}}), .b(Pointer_q), .out(adder_1_out), .cin(not_1_out));  // open: cout
  Adder #(.width(16)) adder_2 (.a(PC_q), .b({16{1'b0}}), .out(adder_2_out), .cin(1'b1));  // open: cout
  Multiplexer #(.enable("false"), .width(16)) multiplexer_1 (
    .in0(adder_2_out), .in1(bit_extender_1_out), .out(multiplexer_1_out), .sel(and_1_out));
  and and_1 (and_1_out, xor_1_out, decoder_jump);
  xor xor_1 (xor_1_out, decoder_loopback, and_3_out);
  Debouncer dbcr (.Pulse(dbcr_pulse), .Buttn(Input_valid), .Clk(Clk), .Rst(Rst));
  Decode decoder (
    .Opcode(program_data), .PtrOp(decoder_ptrop[15]), .MemOp(decoder_memop[7]), .LoopBack(decoder_loopback),
    .MemSrc(decoder_memsrc), .ModPtr(decoder_modptr), .Jump(decoder_jump), .Outp(out_enable),
    .ModMem(decoder_modmem), .Hold(decoder_hold));
  Register #(.width(16)) Pointer (.D(adder_1_out), .en(decoder_modptr), .clk(Clk), .Q(Pointer_q), .clr(Rst));
  or or_1 (or_1_out, dbcr_pulse, not_2_out);
  not not_2 (not_2_out, decoder_hold);
  Register #(.width(16)) PC (.D(multiplexer_1_out), .en(or_1_out), .clk(Clk), .Q(PC_q), .clr(Rst));
  not not_3 (not_3_out, decoder_modptr);
  or or_2 (or_2_out, not_3_out, Clk);
  Multiplexer #(.enable("false"), .width(16)) multiplexer_2 (
    .in0(adder_1_out), .in1(Pointer_q), .out(multiplexer_2_out), .sel(or_2_out));
  ROM #(.addrWidth(16), .dataWidth(16)) \program  (.addr(PC_q), .data({program_data_2, program_data}));
  RAM #(.addrWidth(16)) mem (
    .addr(multiplexer_2_out), .we(decoder_modmem), .oe(1'b1), .clk(Clk), .din(multiplexer_3_out),
    .dout({mem_dout[7], Char_out}));
  assign bit_extender_1_out = {{3{1'b0}}, program_data_2};  // Bit_Extender bit_extender_1
  nor nor_1 (nor_1_out, mem_dout[7], Char_out[6]);
  nor nor_2 (nor_2_out, Char_out[5], Char_out[4]);
  nor nor_3 (nor_3_out, Char_out[3], Char_out[2]);
  nor nor_4 (nor_4_out, Char_out[1], Char_out[0]);
  not not_4 (not_4_out, decoder_memop[7]);
  Adder adder_3 (
    .a({mem_dout[7], Char_out}), .b({8{decoder_memop[7]}}), .out(adder_3_out), .cin(not_4_out));  // open: cout
  and and_2 (and_2_out, nor_1_out, nor_2_out);
  and and_3 (and_3_out, and_2_out, and_4_out);
  and and_4 (and_4_out, nor_3_out, nor_4_out);
  Multiplexer #(.enable("false"), .width(8)) multiplexer_3 (
    .in0(adder_3_out), .in1(Key), .out(multiplexer_3_out), .sel(decoder_memsrc));

  // Notes on the sheet:
  //   contents of program (hex, n*v repeats v):
  //   0 1 4*0 2 2 0 2 0 2 2 0 2 0 0 2 2 1 1 1dcc 3 3 174 2 12c 2 2 2 4*1 3 3 d5 2 2 4*0 3 3 c5 2 1ac 4*1
  //   17d 0 20c 0 1f4 4*0 1c5 2 1 1b5 0 3 4*1 26c 4*1 23d 4*0 3bc 0 0 2d4 4*0 2a5 4*1 384 35c 4*0 2 4*1 3
  //   2fd 4*1 2f5 6*0 28d 0 0 3fc 4*0 3cd 4*1 45c 1 1 2 1 2 1 41d 1 1 a2c 6*0 534 50c 4*1 2 4*0 3 4ad 4*0
  //   4a5 8*1 5a4 4*1 575 0 0 3 5fc 1 1 2 0 0 3 5bd 2 1 1 7dc 3 4*0 784 3 694 2 4*0 3 655 3 1 1 3 6ec 4*0
  //   3 6b5 2 2 0 0 2 754 3 4*1 2 715 2 4*0 645 4*1 7d4 4*1 7a5 615 0 82c 3 824 1 2 0 3 7f5 7e5 2 1 a14 3
  //   4*0 9bc 3 8bc 2 4*0 3 87d 3 1 1 1 3 91c 4*0 3 8e5 2 2 0 0 0 2 98c 3 4*1 2 94d 2 4*0 86d 4*1 a0c 4*1
  //   9dd 83d 1 1 46d 0 0 0 2 a7c 4*0 a4d 3 acc 2 4*1 3 3 a85 2 2 b0c 4*1 add 0 0 0 2 1da4 0 3 df4 0 0 d2c
  //   3 3 bcc 2 2 0 0 2 0 0 3 3 b75 3 1 c8c 3 c84 3 c4c 2 2 2 4*1 3 bfd 2 4*0 3 bed bdd 2 2 0 2 cec 3 4*1
  //   2 cad 2 2 0 0 2 0 0 b5d 1 1 3 4*1 dc4 0 dac 1 3 1 1 1 d75 2 1 d65 0 3 0 0 0 b45 2 0 e34 4*0 e05 3
  //   e84 2 4*1 3 3 e3d 2 2 1 11d4 ed4 4*0 ea5 4*1 11cc 3 106c 3 0 3 3 f5c 1 3 0 2 f2d 2 2 1 102c fac 0 3
  //   1 2 f7d 2 2 fec 4*1 fbd 2 0 0 2 0 0 3 f75 2 2 4*1 3 f05 0 3 115c 2 10e4 1 2 10d4 4*1 10a5 0 108d 0 0
  //   0 1114 3 10fd 0 3 1154 1 2 0 3 1125 107d 2 1 119c 0 2 1 3 116d 2 4*1 ef5 e9d 0 120c 4*1 11dd 0 1bac
  //   3 1b4c 3 16b4 3 0 3 129c 1 1 2 0 2 0 3 1255 6*2 1334 1 8*2 0 3 12cd 1 6 3 3 1 138c 0 3 1 3 135d 5*0
  //   3 3 13dc 1 13c5 1 1 141c 1 1 6 1 13ed 0 143c 3 1425 0 0 3 0 0 2 2 1684 14ac 4*0 147d 2 1664 3 1634 3
  //   4*0 2 8*0 3 15ec 3 15b4 2 2 2 4*1 15ac 3 1595 1555 2 4*0 3 1545 2 2 162c 4*1 15fd 14c5 2 4*1 14b5 0
  //   0 0 1475 2 1 2 1 1 1235 0 1954 3 1944 3 0 18a4 3 3 174c 2 2 4*0 3 3 16fd 3 0 180c 3 1804 3 17cc 2 2
  //   2 4*1 3 177d 2 4*0 3 176d 175d 2 2 1 2 186c 3 4*1 2 182d 2 2 4*0 16e5 4*1 191c 0 1904 4*1 18d5 2 1
  //   18c5 0 3 0 0 16cd 1 16bd 4*0 1ae4 3 3 19dc 2 2 4*0 3 3 198d 3 1 3 3 1a54 2 2 2 4*0 3 3 19fd 2 0 2
  //   1aac 3 4*1 2 1a6d 2 2 4*0 1975 5*1 1b3c 4*1 1b0d 1 1225 0 1b9c 0 2 1 1 2 2 1 1b55 1 1215 0 1d8c 2 0
  //   1d3c 3 3 1c34 2 2 4*0 3 3 1be5 3 0 3 3 1cac 2 2 2 4*0 3 3 1c55 2 1 2 1d04 3 4*1 2 1cc5 2 2 4*0 1bcd
  //   1 1 1 1d84 4*1 1d55 1bb5 0 0 b2d 4*0 ad 7 6 7 6 ffff
endmodule
